// Logisim project 4bitCpu.circ as structural Verilog: 1 circuit, main circuit main
module main (
);

  wire Add, and_1_out, ChangeRomSec, CL, clock_2_out, comparator_1_eq, decoder_1_out0, decoder_1_out13,
       decoder_1_out14, decoder_1_out15, JMP, JMPifA0, LDI, LoadRamBank, LoadRamIntoAFromAdrr, MOV, or_1_out,
       or_2_out, register_1_q, register_2_q, register_3_q, register_4_q, Sub, undriven, writeAintoRamAtAdrr,
       WriteVRam;
  wire [3:0] adder_1_out, Addout, controlled_buffer_1_out, counter_2_q, Operand, outA, outB, RamBankAdr,
       RamOut, RomSec, SubOut, subtractor_1_out;
  wire [7:0] counter_1_q, rom_1_data;
  wire [7:4] register_5_q;

  Comparator #(.width(4)) comparator_1 (.a(outA), .b(4'b0000), .eq(comparator_1_eq));  // open: gt, lt
  and and_1 (and_1_out, JMPifA0, comparator_1_eq);
  or or_1 (or_1_out, and_1_out, JMP);
  Clock #(.highDuration(5), .lowDuration(5)) clock_1 (.out(CL));
  Clock clock_2 (.out(clock_2_out));
  Counter counter_1 (
    .clr(1'b0), .load(or_1_out), .up(1'b1), .clk(CL), .D({RomSec, Operand}), .Q(counter_1_q));  // open: count, carry
  Counter #(.max('hf), .width(4)) counter_2 (
    .clr(undriven), .load(WriteVRam), .up(1'b1), .clk(clock_2_out), .D(Operand), .Q(counter_2_q));  // open: count, carry
  Register #(.width(1)) register_1 (.D(WriteVRam), .en(1'b1), .clk(clock_2_out), .Q(register_1_q));  // open: clr
  Register #(.width(1)) register_2 (.D(Add), .en(1'b1), .clk(CL), .Q(register_2_q));  // open: clr
  Register #(.width(1)) register_3 (.D(Sub), .en(1'b1), .clk(CL), .Q(register_3_q));  // open: clr
  Register #(.width(1)) register_4 (.D(LoadRamIntoAFromAdrr), .en(1'b1), .clk(CL), .Q(register_4_q));  // open: clr
  RAM #(.dataWidth(4)) GeneralRam (
    .addr({Operand, RamBankAdr}), .we(writeAintoRamAtAdrr), .oe(LoadRamIntoAFromAdrr), .clk(CL), .din(outA),
    .dout(RamOut));
  ROM rom_1 (.addr(counter_1_q), .data(rom_1_data));
  RAM #(.addrWidth(4), .dataWidth(4)) VRam (
    .addr(counter_2_q), .we(register_1_q), .oe(1'b1), .clk(clock_2_out), .din(outA));  // open: dout
  assign controlled_buffer_1_out = register_2_q ? Addout : 4'bz;  // Controlled_Buffer controlled_buffer_1
  assign controlled_buffer_1_out = register_3_q ? SubOut : 4'bz;  // Controlled_Buffer controlled_buffer_2
  assign controlled_buffer_1_out = register_4_q ? RamOut : 4'bz;  // Controlled_Buffer controlled_buffer_3
  assign controlled_buffer_1_out = LDI ? Operand : 4'bz;  // Controlled_Buffer controlled_buffer_4
  or or_2 (or_2_out, register_2_q, register_3_q, register_4_q, LDI);
  Register register_5 (.D(rom_1_data), .en(1'b1), .clk(CL), .Q({register_5_q, Operand}), .clr(1'b0));
  Register #(.width(4)) B (.D(outA), .en(MOV), .clk(CL), .Q(outB));  // open: clr
  Register #(.width(4)) A (.D(controlled_buffer_1_out), .en(or_2_out), .clk(CL), .Q(outA));  // open: clr
  Register #(.width(4)) RamBankAdress (.D(Operand), .en(LoadRamBank), .clk(CL), .Q(RamBankAdr));  // open: clr
  Register #(.width(4)) u_RomSec (.D(Operand), .en(ChangeRomSec), .clk(CL), .Q(RomSec));  // open: clr
  // DotMatrix #(.inputtype("select"), .matrixcols(8), .matrixrows(8)) dotmatrix_1: pin names not known
  LED led_1 (.in(decoder_1_out0));
  LED led_2 (.in(MOV));
  LED led_3 (.in(decoder_1_out13));
  LED led_4 (.in(decoder_1_out14));
  LED led_5 (.in(decoder_1_out15));
  Decoder #(.select(4)) decoder_1 (
    .out0(decoder_1_out0), .out1(LDI), .out2(Add), .out3(Sub), .out4(MOV), .out5(MOV), .out6(JMP),
    .out7(JMPifA0), .out8(ChangeRomSec), .out9(LoadRamBank), .out10(writeAintoRamAtAdrr),
    .out11(LoadRamIntoAFromAdrr), .out12(WriteVRam), .out13(decoder_1_out13), .out14(decoder_1_out14),
    .out15(decoder_1_out15), .sel(register_5_q), .en(1'b1));
  Adder #(.width(4)) adder_1 (.a(outA), .b(outB), .out(adder_1_out));  // open: cin, cout
  Subtractor #(.width(4)) subtractor_1 (.a(outA), .b(outB), .out(subtractor_1_out));  // open: bin, bout
  Register #(.width(4)) register_6 (.D(adder_1_out), .en(Add), .clk(CL), .Q(Addout));  // open: clr
  Register #(.width(4)) register_7 (.D(subtractor_1_out), .en(Sub), .clk(CL), .Q(SubOut));  // open: clr

  // Notes on the sheet:
  //   contents of rom_1 (hex, n*v repeats v):
  //   13 c0 19 c2 0 0 a0 10 0 b0 0 20 0 a0 0 67
  //   Opcode
endmodule
